// Logisim project CombinationLock.circ as structural Verilog: 1 circuit, main circuit main
module main (
);

  wire and_1_out, button_1_out, button_2_out, button_3_out, button_4_out, comparator_1_eq, comparator_2_eq,
       comparator_3_eq, comparator_4_eq, Reset_out;
  wire [3:0] counter_1_q, counter_2_q, counter_3_q, counter_4_q, dipswitch_1_sw4, dipswitch_2_sw4,
       dipswitch_3_sw4, dipswitch_4_sw4;

  Counter #(.max('h9), .width(4)) counter_1 (
    .clr(Reset_out), .clk(button_1_out), .Q(counter_1_q));  // open: load, up, count, D, carry
  Counter #(.max('h9), .width(4)) counter_2 (
    .clr(Reset_out), .clk(button_3_out), .Q(counter_2_q));  // open: load, up, count, D, carry
  Button Reset (.out(Reset_out));
  Hex_Digit_Display hex_digit_display_1 (.value(counter_1_q));  // open: dp
  Button button_1 (.out(button_1_out));
  Hex_Digit_Display hex_digit_display_2 (.value(counter_3_q));  // open: dp
  Hex_Digit_Display hex_digit_display_3 (.value(counter_2_q));  // open: dp
  Button button_2 (.out(button_2_out));
  DipSwitch #(.number(4)) dipswitch_1 (
    .sw1(dipswitch_1_sw4[3]), .sw2(dipswitch_1_sw4[2]), .sw3(dipswitch_1_sw4[1]), .sw4(dipswitch_1_sw4[0]));
  LED Unlocked (.in(and_1_out));
  Hex_Digit_Display hex_digit_display_4 (.value(counter_4_q));  // open: dp
  Button button_3 (.out(button_3_out));
  Button button_4 (.out(button_4_out));
  Comparator #(.width(4)) comparator_1 (.a(dipswitch_1_sw4), .b(counter_1_q), .eq(comparator_1_eq));  // open: gt, lt
  and and_1 (and_1_out, comparator_1_eq, comparator_3_eq, comparator_4_eq, comparator_2_eq);
  Comparator #(.width(4)) comparator_2 (.a(dipswitch_2_sw4), .b(counter_2_q), .eq(comparator_2_eq));  // open: gt, lt
  DipSwitch #(.number(4)) dipswitch_2 (
    .sw1(dipswitch_2_sw4[3]), .sw2(dipswitch_2_sw4[2]), .sw3(dipswitch_2_sw4[1]), .sw4(dipswitch_2_sw4[0]));
  Counter #(.max('h9), .width(4)) counter_3 (
    .clr(Reset_out), .clk(button_2_out), .Q(counter_3_q));  // open: load, up, count, D, carry
  Counter #(.max('h9), .width(4)) counter_4 (
    .clr(Reset_out), .clk(button_4_out), .Q(counter_4_q));  // open: load, up, count, D, carry
  DipSwitch #(.number(4)) dipswitch_3 (
    .sw1(dipswitch_3_sw4[3]), .sw2(dipswitch_3_sw4[2]), .sw3(dipswitch_3_sw4[1]), .sw4(dipswitch_3_sw4[0]));
  Comparator #(.width(4)) comparator_3 (.a(dipswitch_4_sw4), .b(counter_3_q), .eq(comparator_3_eq));  // open: gt, lt
  DipSwitch #(.number(4)) dipswitch_4 (
    .sw1(dipswitch_4_sw4[3]), .sw2(dipswitch_4_sw4[2]), .sw3(dipswitch_4_sw4[1]), .sw4(dipswitch_4_sw4[0]));
  Comparator #(.width(4)) comparator_4 (.a(dipswitch_3_sw4), .b(counter_4_q), .eq(comparator_4_eq));  // open: gt, lt
endmodule
